# Fritzing sketch Simon Dice (saved by Fritzing 0.9.4)
breadboards: 1

parts:
  HC-SR04_Sensor_2 = HC-SR04 Ultrasonic Distance Sensor
  HC-SR04_Sensor_3 = HC-SR04 Ultrasonic Distance Sensor
  HC-SR04_Sensor_4 = HC-SR04 Ultrasonic Distance Sensor
  HC-SR04_Sensor_5 = HC-SR04 Ultrasonic Distance Sensor
  Componente1 = Arduino Uno (Rev3) - ICSP
  LED3 = smd LED [color="Red (633nm)" package="1206 [SMD]"]
  R4 = Resistor [tolerance=±5% resistance=100 package=THT]
  R5 = Resistor [tolerance=±5% resistance=100 package=THT]
  LED4 = smd LED [color="Blue (430nm)" package="1206 [SMD]"]
  R6 = Resistor [tolerance=±5% resistance=100 package=THT]
  LED5 = smd LED [color="Yellow (585nm)" package="1206 [SMD]"]
  R7 = Resistor [tolerance=±5% resistance=100 package=THT]
  LED6 = smd LED [color="Green (555nm)" package="1206 [SMD]"]
  J1 = Piezo Speaker

nets:
  VCC: HC-SR04_Sensor_2.VCC, HC-SR04_Sensor_3.VCC, HC-SR04_Sensor_4.VCC, HC-SR04_Sensor_5.VCC, Componente1.5V
  N1: HC-SR04_Sensor_2.TRIG, Componente1.D7
  N2: HC-SR04_Sensor_2.ECHO, Componente1.D3_PWM
  GND: HC-SR04_Sensor_2.GND, HC-SR04_Sensor_3.GND, HC-SR04_Sensor_4.GND, HC-SR04_Sensor_5.GND, Componente1.GND, LED3.cathode, LED4.cathode, LED5.cathode, LED6.cathode, J1.pin1
  N3: HC-SR04_Sensor_3.TRIG, Componente1.D4
  N4: HC-SR04_Sensor_3.ECHO, Componente1.D0/RX
  N5: HC-SR04_Sensor_4.TRIG, Componente1.D5_PWM
  N6: HC-SR04_Sensor_4.ECHO, Componente1.D1/TX
  N7: HC-SR04_Sensor_5.TRIG, Componente1.D6_PWM
  N8: HC-SR04_Sensor_5.ECHO, Componente1.D2
  N9: Componente1.ICSP_MOSI, Componente1.D11_PWM/MOSI, R4.Pin_1
  N10: Componente1.D8, R7.Pin_1
  N11: Componente1.D9_PWM, R6.Pin_1
  N12: Componente1.D10_PWM/SS, R5.Pin_1
  N13: Componente1.D12/MISO, J1.pin2
  N14: LED3.anode, R4.Pin_0
  N15: R5.Pin_0, LED4.anode
  N16: R6.Pin_0, LED5.anode
  N17: R7.Pin_0, LED6.anode
